# Fritzing sketch datavault_schematics (saved by Fritzing 0.9.9b)
breadboards: 2

parts:
  M1 = RioRand LM2596
  J2 = Power Jack [package=power_jack_pth]
  Raspberry_Pi1 = Raspberry Pi B+
  U1 = ESP8266 NodeMCU LoLin module
  GV5-1 = Omron_MY2K_02_12VDC_3A [part_number=GV5-2 package=THT]
  LED1 = smd LED [color="Green (555nm)" package="0603 [SMD]"]
  LED2 = smd LED [color="Red (633nm)" package="0603 [SMD]"]
  R1 = Resistor [tolerance=±5% power=0.25 resistance=220 package=THT]
  R2 = Resistor [tolerance=±5% power=0.25 resistance=220 package=THT]
  S1 = Momentary Switch [package=ksa_sealed_tac_switch]
  S2 = Momentary Switch [package=ksa_sealed_tac_switch]
  J3 = COMPUTER-PERIPHERAL-POWER [package=computer-peripheral-power]
  D2 = Rectifier Diode [part_number=1N4001 package="300 mil [THT]"]
  Q1 = TRANSISTOR_NPN [package=to-92-ammo]
  R3 = Resistor [tolerance=±5% power=0.25 resistance=1k package=THT]

nets:
  N1: M1.Pin_1, J2.PWR, GV5-1.Out_2-2, GV5-1.Set/Reset#90, D2.cathode
  N2: M1.Pin_2, J2.GND
  N3: M1.Pin_3, U1.Vin, GV5-1.Out_2-1
  GND: M1.Pin_4, Raspberry_Pi1.GND, U1.GND, R1.Pin_1, R2.Pin_1, S1.4, S2.4, J3.GND, Q1.E
  N4: Raspberry_Pi1.GPIO15, U1.D2
  N5: Raspberry_Pi1.GPIO14, U1.D1
  N6: U1.D0, LED1.anode
  N7: U1.D5, S1.2
  N8: U1.D6, S2.2
  N9: U1.D7, LED2.anode
  N10: U1.D8, R3.Pin_0
  N11: GV5-1.Out_1-1, J3.5V
  N12: GV5-1.Out_1-2, J3.12V
  N13: GV5-1.Set/Reset#89, D2.anode, Q1.C
  N14: LED1.cathode, R2.Pin_0
  N15: LED2.cathode, R1.Pin_0
  N16: Q1.B, R3.Pin_1

notes:
  SATA HDD power
  5V DC regulator
  12V in
  relay board

custom parts:
  ESP8266 NodeMCU LoLin module: ESP8266 based NodeMCU
  Omron_MY2K_02_12VDC_3A: Omron GV5-2, 12VDC @ 2 Amp, Bistable, Low Signal Relay, DPDT, No Coil Polarity
